// Logisim project Exercicio Pratico 01.circ as structural Verilog: 6 circuits, main circuit main
module main (
  input  A0,
  input  Ci,
  input  A1,
  input  A2,
  input  A3,
  input  B0,
  input  B1,
  input  B2,
  input  B3,
  output S0,
  output S1,
  output S2,
  output S3,
  output Overflow,
  output Co
);

  wire decodificador_1_l0, decodificador_1_l1, decodificador_1_l2, decodificador_1_l3, decodificador_1_l4,
       decodificador_1_l5, decodificador_1_l6, decodificador_1_l7, decodificador_2_l0, decodificador_2_l1,
       decodificador_2_l2, decodificador_2_l3, decodificador_2_l4, decodificador_2_l5, decodificador_2_l6,
       decodificador_2_l7, decodificador_3_l0, decodificador_3_l1, decodificador_3_l2, decodificador_3_l3,
       decodificador_3_l4, decodificador_3_l5, decodificador_3_l6, decodificador_3_l7;

  Decodificador decodificador_1 (
    .A3(A0), .A2(A1), .A1(A2), .A0(A3), .L0(decodificador_1_l0), .L1(decodificador_1_l1),
    .L2(decodificador_1_l2), .L3(decodificador_1_l3), .L4(decodificador_1_l4), .L5(decodificador_1_l5),
    .L6(decodificador_1_l6), .L7(decodificador_1_l7));
  Decodificador decodificador_2 (
    .A3(B0), .A2(B1), .A1(B2), .A0(B3), .L0(decodificador_2_l0), .L1(decodificador_2_l1),
    .L2(decodificador_2_l2), .L3(decodificador_2_l3), .L4(decodificador_2_l4), .L5(decodificador_2_l5),
    .L6(decodificador_2_l6), .L7(decodificador_2_l7));
  _7_Segment_Display u_7_segment_display_1 (
    .g(decodificador_1_l3), .f(decodificador_1_l2), .a(decodificador_1_l1), .b(decodificador_1_l0),
    .e(decodificador_1_l4), .d(decodificador_1_l5), .c(decodificador_1_l6), .dp(decodificador_1_l7));
  Somador_4bits_Overflow somador_4bits_overflow_1 (
    .A3(A0), .A2(A1), .A1(A2), .A0(A3), .B3(B0), .B2(B1), .B1(B2), .B0(B3), .S0(S3), .S1(S2), .S2(S1),
    .S3(S0), .Overflow(Overflow), .Ci(Ci), .Co(Co));
  _7_Segment_Display u_7_segment_display_2 (
    .g(decodificador_2_l3), .f(decodificador_2_l2), .a(decodificador_2_l1), .b(decodificador_2_l0),
    .e(decodificador_2_l4), .d(decodificador_2_l5), .c(decodificador_2_l6), .dp(decodificador_2_l7));
  Decodificador decodificador_3 (
    .A3(S0), .A2(S1), .A1(S2), .A0(S3), .L0(decodificador_3_l0), .L1(decodificador_3_l1),
    .L2(decodificador_3_l2), .L3(decodificador_3_l3), .L4(decodificador_3_l4), .L5(decodificador_3_l5),
    .L6(decodificador_3_l6), .L7(decodificador_3_l7));
  _7_Segment_Display u_7_segment_display_3 (
    .g(decodificador_3_l3), .f(decodificador_3_l2), .a(decodificador_3_l1), .b(decodificador_3_l0),
    .e(decodificador_3_l4), .d(decodificador_3_l5), .c(decodificador_3_l6), .dp(decodificador_3_l7));
endmodule

module Somador_1_2 (
  input  A,
  input  B,
  output Soma,
  output Vai_1
);

  and and_1 (Vai_1, A, B);
  xor xor_1 (Soma, A, B);
endmodule

module Somador_2bits (
  input  Primeiro,
  input  A,
  input  B,
  output Soma,
  output Vai_1
);

  wire somador_1_2_1_soma, somador_1_2_1_vai_1, somador_1_2_2_vai_1;

  Somador_1_2 somador_1_2_1 (.A(A), .B(B), .Vai_1(somador_1_2_1_vai_1), .Soma(somador_1_2_1_soma));
  or or_1 (Vai_1, somador_1_2_1_vai_1, somador_1_2_2_vai_1);
  Somador_1_2 somador_1_2_2 (.A(Primeiro), .B(somador_1_2_1_soma), .Vai_1(somador_1_2_2_vai_1), .Soma(Soma));
endmodule

module Somador_4bits (
  input  Ci,
  input  A3,
  input  A2,
  input  A1,
  input  A0,
  input  B3,
  input  B2,
  input  B1,
  input  B0,
  output S0,
  output S1,
  output S2,
  output S3,
  output Co
);

  wire somador_2bits_1_vai_1, somador_2bits_2_vai_1, somador_2bits_3_vai_1;

  Somador_2bits somador_2bits_1 (.A(A0), .B(B0), .Primeiro(Ci), .Vai_1(somador_2bits_1_vai_1), .Soma(S0));
  Somador_2bits somador_2bits_2 (
    .A(A1), .B(B1), .Primeiro(somador_2bits_1_vai_1), .Vai_1(somador_2bits_2_vai_1), .Soma(S1));
  Somador_2bits somador_2bits_3 (
    .A(A2), .B(B2), .Primeiro(somador_2bits_2_vai_1), .Vai_1(somador_2bits_3_vai_1), .Soma(S2));
  Somador_2bits somador_2bits_4 (.A(A3), .B(B3), .Primeiro(somador_2bits_3_vai_1), .Vai_1(Co), .Soma(S3));
endmodule

// Somador 4 bits
module Somador_4bits_Overflow (
  input  Ci,
  input  A3,
  input  A2,
  input  A1,
  input  A0,
  input  B3,
  input  B2,
  input  B1,
  input  B0,
  output S0,
  output S1,
  output S2,
  output S3,
  output Overflow,
  output Co
);

  wire or_1_out, somador_2bits_1_vai_1, somador_2bits_2_vai_1, somador_2bits_3_vai_1;

  Somador_2bits somador_2bits_1 (.A(A0), .B(B0), .Primeiro(Ci), .Vai_1(somador_2bits_1_vai_1), .Soma(S0));
  Somador_2bits somador_2bits_2 (
    .A(A1), .B(B1), .Primeiro(somador_2bits_1_vai_1), .Vai_1(somador_2bits_2_vai_1), .Soma(S1));
  Somador_2bits somador_2bits_3 (
    .A(A2), .B(B2), .Primeiro(somador_2bits_2_vai_1), .Vai_1(somador_2bits_3_vai_1), .Soma(S2));
  Somador_2bits somador_2bits_4 (.A(A3), .B(B3), .Primeiro(somador_2bits_3_vai_1), .Vai_1(Co), .Soma(S3));
  or or_1 (or_1_out, S3, S2, S1, S0);
  and and_1 (Overflow, or_1_out, Co);
endmodule

module Decodificador (
  input  A3,
  input  A2,
  input  A1,
  input  A0,
  output L0,
  output L1,
  output L2,
  output L3,
  output L4,
  output L5,
  output L6,
  output L7
);

  wire and_1_out, and_2_out, and_3_out, and_4_out, and_5_out, and_6_out, and_7_out, and_8_out, and_9_out,
       and_10_out, and_11_out, and_12_out, and_13_out, and_14_out, and_15_out, and_16_out, and_17_out,
       and_18_out, and_19_out, and_20_out, and_21_out, and_22_out, and_23_out, and_24_out, and_25_out,
       and_26_out, and_27_out, and_28_out, and_29_out, and_30_out, and_31_out, and_32_out, and_33_out,
       and_34_out, and_35_out, and_36_out, and_37_out, and_38_out, and_39_out, and_40_out, and_41_out,
       and_42_out, and_43_out, and_44_out, and_45_out, not_1_out, not_2_out, not_3_out, not_4_out, not_5_out,
       not_6_out, not_7_out, not_8_out, not_9_out, not_10_out, not_11_out, not_12_out, not_13_out,
       not_14_out, not_15_out, not_16_out, not_17_out, not_18_out, not_19_out, not_20_out, not_21_out,
       not_22_out, not_23_out, not_24_out, not_25_out, not_26_out, not_27_out, not_28_out, not_29_out,
       not_30_out, not_31_out, not_32_out, not_33_out, not_34_out, not_35_out, not_36_out, not_37_out,
       not_38_out, not_39_out, not_40_out, not_41_out, not_42_out, or_1_out, or_2_out, or_3_out, or_4_out,
       or_5_out, or_6_out, or_7_out, or_8_out, or_9_out, or_11_out, or_12_out, or_14_out, or_15_out,
       or_16_out, or_17_out, or_18_out, or_19_out, or_20_out, or_22_out, or_23_out;

  not not_1 (not_1_out, A3);
  not not_2 (not_2_out, A2);
  not not_3 (not_3_out, A3);
  and and_1 (and_1_out, not_3_out, not_4_out);
  not not_4 (not_4_out, A1);
  not not_5 (not_5_out, A0);
  not not_6 (not_6_out, A3);
  not not_7 (not_7_out, A1);
  not not_8 (not_8_out, A2);
  not not_9 (not_9_out, A0);
  not not_10 (not_10_out, A3);
  not not_11 (not_11_out, A3);
  and and_2 (and_2_out, A3, not_12_out);
  not not_12 (not_12_out, A2);
  not not_13 (not_13_out, A1);
  not not_14 (not_14_out, A1);
  and and_3 (and_3_out, not_14_out, not_15_out);
  not not_15 (not_15_out, A0);
  not not_16 (not_16_out, A3);
  and and_4 (and_4_out, not_16_out, A2);
  and and_5 (and_5_out, A3, not_17_out);
  not not_17 (not_17_out, A2);
  and and_6 (and_6_out, A3, A1);
  not not_18 (not_18_out, A2);
  and and_7 (and_7_out, not_18_out, A1);
  and and_8 (and_8_out, A1, not_19_out);
  not not_19 (not_19_out, A0);
  not not_20 (not_20_out, A3);
  and and_9 (and_9_out, not_20_out, A2);
  not not_21 (not_21_out, A1);
  not not_22 (not_22_out, A2);
  not not_23 (not_23_out, A2);
  and and_10 (and_10_out, not_23_out, not_24_out);
  not not_24 (not_24_out, A0);
  and and_11 (and_11_out, A1, not_25_out);
  not not_25 (not_25_out, A0);
  and and_12 (and_12_out, A3, A1);
  and and_13 (and_13_out, A3, A2);
  not not_26 (not_26_out, A3);
  and and_14 (and_14_out, not_26_out, not_27_out);
  not not_27 (not_27_out, A2);
  not not_28 (not_28_out, A0);
  not not_29 (not_29_out, A2);
  and and_15 (and_15_out, not_29_out, A1);
  not not_30 (not_30_out, A1);
  not not_31 (not_31_out, A1);
  not not_32 (not_32_out, A3);
  and and_16 (and_16_out, not_32_out, not_33_out);
  not not_33 (not_33_out, A1);
  not not_34 (not_34_out, A3);
  and and_17 (and_17_out, not_34_out, A0);
  not not_35 (not_35_out, A1);
  not not_36 (not_36_out, A3);
  not not_37 (not_37_out, A2);
  and and_18 (and_18_out, not_1_out, not_2_out);
  and and_19 (and_19_out, and_1_out, not_5_out);
  not not_38 (not_38_out, A2);
  not not_39 (not_39_out, A0);
  and and_20 (and_20_out, not_6_out, A1);
  and and_21 (and_21_out, A3, not_7_out);
  and and_22 (and_22_out, not_8_out, not_9_out);
  and and_23 (and_23_out, not_10_out, A1);
  and and_24 (and_24_out, not_11_out, A2);
  and and_25 (and_25_out, A2, A1);
  and and_26 (and_26_out, and_2_out, not_13_out);
  not not_40 (not_40_out, A0);
  or or_1 (or_1_out, and_3_out, and_4_out);
  or or_2 (or_2_out, and_5_out, and_6_out);
  or or_3 (or_3_out, and_7_out, and_8_out);
  and and_27 (and_27_out, and_9_out, not_21_out);
  and and_28 (and_28_out, A3, not_22_out);
  and and_29 (and_29_out, A3, A0);
  or or_4 (or_4_out, and_10_out, and_11_out);
  or or_5 (or_5_out, and_12_out, and_13_out);
  and and_30 (and_30_out, and_14_out, not_28_out);
  and and_31 (and_31_out, and_15_out, A0);
  and and_32 (and_32_out, A2, not_30_out);
  and and_33 (and_33_out, A2, A1);
  not not_41 (not_41_out, A0);
  and and_34 (and_34_out, A3, not_31_out);
  not not_42 (not_42_out, A0);
  or or_6 (or_6_out, and_16_out, and_17_out);
  and and_35 (and_35_out, not_35_out, A0);
  and and_36 (and_36_out, not_36_out, A2);
  and and_37 (and_37_out, A3, not_37_out);
  or or_7 (or_7_out, and_18_out, and_19_out);
  and and_38 (and_38_out, not_38_out, not_39_out);
  and and_39 (and_39_out, and_20_out, A0);
  and and_40 (and_40_out, and_21_out, A0);
  or or_8 (or_8_out, and_22_out, and_23_out);
  and and_41 (and_41_out, and_24_out, A0);
  or or_9 (or_9_out, and_25_out, and_26_out);
  and and_42 (and_42_out, A3, not_40_out);
  or or_10 (L2, or_1_out, or_2_out);
  or or_11 (or_11_out, or_3_out, and_27_out);
  or or_12 (or_12_out, and_28_out, and_29_out);
  or or_13 (L4, or_4_out, or_5_out);
  or or_14 (or_14_out, and_30_out, and_31_out);
  and and_43 (and_43_out, and_32_out, A0);
  and and_44 (and_44_out, and_33_out, not_41_out);
  and and_45 (and_45_out, and_34_out, not_42_out);
  or or_15 (or_15_out, or_6_out, and_35_out);
  or or_16 (or_16_out, and_36_out, and_37_out);
  or or_17 (or_17_out, or_7_out, and_38_out);
  or or_18 (or_18_out, and_39_out, and_40_out);
  or or_19 (or_19_out, or_8_out, and_41_out);
  or or_20 (or_20_out, or_9_out, and_42_out);
  or or_21 (L3, or_11_out, or_12_out);
  or or_22 (or_22_out, or_14_out, and_43_out);
  or or_23 (or_23_out, and_44_out, and_45_out);
  or or_24 (L6, or_15_out, or_16_out);
  or or_25 (L0, or_17_out, or_18_out);
  or or_26 (L1, or_19_out, or_20_out);
  or or_27 (L5, or_22_out, or_23_out);

  assign L7 = 1'b0;
endmodule
