// Logisim project Exercício Pratico 02.circ as structural Verilog
module B_invert (
  input  Operation,
  input  BA,
  input  BB,
  output out_4
);

  wire and_1_out, and_2_out, not_1_out;

  and and_1 (and_1_out, BA, not_1_out);
  not not_1 (not_1_out, Operation);
  and and_2 (and_2_out, Operation, BB);
  or or_1 (out_4, and_1_out, and_2_out);
endmodule

module Mux_4_bits (
  input  Operation,
  input  Operation_2,
  input  A,
  input  B,
  input  C,
  input  D,
  output Result
);

  wire and_1_out, and_2_out, and_3_out, and_4_out, not_1_out, not_2_out, not_3_out, not_4_out;

  not not_1 (not_1_out, Operation);
  not not_2 (not_2_out, Operation_2);
  not not_3 (not_3_out, Operation);
  not not_4 (not_4_out, Operation_2);
  and and_1 (and_1_out, A, not_1_out, not_2_out);
  and and_2 (and_2_out, B, not_3_out, Operation_2);
  and and_3 (and_3_out, C, Operation, not_4_out);
  and and_4 (and_4_out, D, Operation, Operation_2);
  or or_1 (Result, and_1_out, and_2_out, and_3_out, and_4_out);
endmodule

module meio_somador (
  input  A,
  input  B,
  output S,
  output Carry_out
);

  xor xor_1 (S, A, B);
  and and_1 (Carry_out, B, A);
endmodule

module Somador_completo1bit (
  input  A,
  input  B,
  input  C,
  output S0,
  output C0
);

  wire meio_somador_1_carry_out, meio_somador_1_s, meio_somador_2_carry_out;

  meio_somador meio_somador_1 (.A(A), .B(B), .S(meio_somador_1_s), .Carry_out(meio_somador_1_carry_out));
  meio_somador meio_somador_2 (.A(meio_somador_1_s), .B(C), .S(S0), .Carry_out(meio_somador_2_carry_out));
  or or_1 (C0, meio_somador_2_carry_out, meio_somador_1_carry_out);
endmodule

module ULA_1bit (
  input  Controlador,
  input  Carry_In,
  input  Operation_1,
  input  Operation_2,
  input  A,
  input  B,
  output Resultado,
  output Carry_out
);

  wire and_1_out, b_invert_1_out_4, not_1_out, not_2_out, or_1_out, somador_completo1bit_1_s0;

  not not_1 (not_1_out, B);
  B_invert b_invert_1 (.BA(B), .BB(not_1_out), .Operation(Controlador), .out_4(b_invert_1_out_4));
  and and_1 (and_1_out, A, b_invert_1_out_4);
  or or_1 (or_1_out, A, b_invert_1_out_4);
  not not_2 (not_2_out, A);
  Somador_completo1bit somador_completo1bit_1 (
    .A(A), .B(b_invert_1_out_4), .C(Carry_In), .S0(somador_completo1bit_1_s0), .C0(Carry_out));
  Mux_4_bits mux_4_bits_1 (
    .A(and_1_out), .B(or_1_out), .C(not_2_out), .D(somador_completo1bit_1_s0), .Operation(Operation_1),
    .Operation_2(Operation_2), .Result(Resultado));

  // Notes on the sheet:
  //   +
endmodule

module ULA_4_bits (
  input  Binvert,
  input  Op1,
  input  Op2,
  input  B3,
  input  B2,
  input  B1,
  input  B0,
  input  A3,
  input  A2,
  input  A1,
  input  A0,
  output S0,
  output S0_2,
  output S0_3,
  output S0_4,
  output Cout
);

  wire ula_1bit_1_carry_out, ula_1bit_2_carry_out, ula_1bit_3_carry_out;

  ULA_1bit ula_1bit_1 (
    .Operation_1(Op1), .A(A0), .B(B0), .Operation_2(Op2), .Resultado(S0), .Controlador(Binvert),
    .Carry_In(Binvert), .Carry_out(ula_1bit_1_carry_out));
  ULA_1bit ula_1bit_2 (
    .Operation_1(Op1), .A(A1), .B(B1), .Operation_2(Op2), .Resultado(S0_2), .Controlador(Binvert),
    .Carry_In(ula_1bit_1_carry_out), .Carry_out(ula_1bit_2_carry_out));
  ULA_1bit ula_1bit_3 (
    .Operation_1(Op1), .A(A2), .B(B2), .Operation_2(Op2), .Resultado(S0_3), .Controlador(Binvert),
    .Carry_In(ula_1bit_2_carry_out), .Carry_out(ula_1bit_3_carry_out));
  ULA_1bit ula_1bit_4 (
    .Operation_1(Op1), .A(A3), .B(B3), .Operation_2(Op2), .Resultado(S0_4), .Controlador(Binvert),
    .Carry_In(ula_1bit_3_carry_out), .Carry_out(Cout));

  // Notes on the sheet:
  //   Cin
  //   Cout
  //   Cout
  //   Cout
  //   ULA0
  //   ULA1
  //   ULA2
  //   ULA3
endmodule
