// Logisim project Logide soma.circ as structural Verilog
module meio_somador (
  input  A,
  input  B,
  output S,
  output Carry_out___vai_1
);

  xor xor_1 (S, A, B);
  and and_1 (Carry_out___vai_1, B, A);
endmodule

module Somador_completo2 (
  input  A,
  input  B,
  input  C,
  output S0,
  output C0
);

  wire meio_somador_1_carry_out___vai_1, meio_somador_1_s, meio_somador_2_carry_out___vai_1;

  meio_somador meio_somador_1 (
    .A(A), .B(B), .S(meio_somador_1_s), .Carry_out___vai_1(meio_somador_1_carry_out___vai_1));
  meio_somador meio_somador_2 (
    .A(meio_somador_1_s), .B(C), .S(S0), .Carry_out___vai_1(meio_somador_2_carry_out___vai_1));
  or or_1 (C0, meio_somador_2_carry_out___vai_1, meio_somador_1_carry_out___vai_1);
endmodule

module somador_de_4bit (
  input  Carry_in,
  input  A1,
  input  B1,
  input  C1,
  input  D1,
  input  A0,
  input  B0,
  input  C0,
  input  D0,
  output Sd,
  output Sc,
  output Sb,
  output Sa,
  output Overflow,
  output Carry_out
);

  wire somador_completo2_1_c0, somador_completo2_2_c0, somador_completo2_3_c0;

  Somador_completo2 somador_completo2_1 (.A(D1), .B(D0), .C(Carry_in), .S0(Sd), .C0(somador_completo2_1_c0));
  Somador_completo2 somador_completo2_2 (
    .A(C1), .B(C0), .C(somador_completo2_1_c0), .S0(Sc), .C0(somador_completo2_2_c0));
  Somador_completo2 somador_completo2_3 (
    .A(B1), .B(B0), .C(somador_completo2_2_c0), .S0(Sb), .C0(somador_completo2_3_c0));
  Somador_completo2 somador_completo2_4 (.A(A1), .B(A0), .C(somador_completo2_3_c0), .S0(Sa), .C0(Carry_out));
  xor xor_1 (Overflow, somador_completo2_3_c0, Carry_out);
endmodule

module Decodificador (
  input  A4,
  input  A3,
  input  A2,
  input  A1,
  output L1,
  output L2,
  output L3,
  output L4,
  output L5,
  output L6,
  output L7
);

  wire and_1_out, and_2_out, and_3_out, and_4_out, and_5_out, and_6_out, and_7_out, and_8_out, and_9_out,
       and_10_out, and_11_out, and_12_out, and_13_out, and_14_out, and_15_out, and_16_out, and_17_out,
       and_18_out, and_19_out, and_20_out, and_21_out, and_22_out, and_23_out, and_24_out, and_25_out,
       and_26_out, and_27_out, and_28_out, and_29_out, and_30_out, and_31_out, and_32_out, and_33_out,
       and_34_out, and_35_out, not_1_out, not_2_out, not_3_out, not_4_out, not_5_out, not_6_out, not_7_out,
       not_8_out, not_9_out, not_10_out, not_11_out, not_12_out, not_13_out, not_14_out, not_15_out,
       not_16_out, not_17_out, not_18_out, not_19_out, not_20_out, not_21_out, not_22_out, not_23_out,
       not_24_out, not_25_out, not_26_out, not_27_out, not_28_out, not_29_out, not_30_out, not_31_out,
       not_32_out, not_33_out, not_34_out, not_35_out, not_36_out, not_37_out, not_38_out, not_39_out,
       not_40_out, not_41_out, not_42_out, not_43_out, not_44_out;

  not not_1 (not_1_out, A4);
  and and_1 (and_1_out, not_1_out, not_2_out);
  not not_2 (not_2_out, A3);
  not not_3 (not_3_out, A4);
  not not_4 (not_4_out, A2);
  and and_2 (and_2_out, not_3_out, not_4_out, not_5_out);
  not not_5 (not_5_out, A1);
  not not_6 (not_6_out, A3);
  and and_3 (and_3_out, not_6_out, not_7_out);
  not not_7 (not_7_out, A1);
  not not_8 (not_8_out, A4);
  and and_4 (and_4_out, not_8_out, A2, A1);
  not not_9 (not_9_out, A2);
  and and_5 (and_5_out, A4, not_9_out, A1);
  not not_10 (not_10_out, A3);
  and and_6 (and_6_out, not_10_out, not_11_out);
  not not_11 (not_11_out, A1);
  not not_12 (not_12_out, A4);
  and and_7 (and_7_out, not_12_out, A2);
  not not_13 (not_13_out, A4);
  and and_8 (and_8_out, not_13_out, A3, A1);
  and and_9 (and_9_out, A3, A2);
  and and_10 (and_10_out, A4, not_14_out, not_15_out);
  not not_14 (not_14_out, A3);
  not not_15 (not_15_out, A2);
  and and_11 (and_11_out, A4, not_16_out);
  not not_16 (not_16_out, A1);
  not not_17 (not_17_out, A2);
  and and_12 (and_12_out, not_17_out, not_18_out);
  not not_18 (not_18_out, A1);
  not not_19 (not_19_out, A4);
  and and_13 (and_13_out, not_19_out, A3, not_20_out);
  not not_20 (not_20_out, A2);
  and and_14 (and_14_out, A3, not_21_out);
  not not_21 (not_21_out, A1);
  and and_15 (and_15_out, A4, not_22_out);
  not not_22 (not_22_out, A3);
  and and_16 (and_16_out, A4, A2);
  not not_23 (not_23_out, A3);
  and and_17 (and_17_out, not_23_out, A2);
  and and_18 (and_18_out, A2, not_24_out);
  not not_24 (not_24_out, A1);
  not not_25 (not_25_out, A4);
  and and_19 (and_19_out, not_25_out, A3, not_26_out);
  not not_26 (not_26_out, A2);
  and and_20 (and_20_out, A4, not_27_out);
  not not_27 (not_27_out, A3);
  and and_21 (and_21_out, A4, A1);
  not not_28 (not_28_out, A3);
  and and_22 (and_22_out, not_28_out, not_29_out);
  not not_29 (not_29_out, A1);
  and and_23 (and_23_out, A2, not_30_out);
  not not_30 (not_30_out, A1);
  and and_24 (and_24_out, A4, A2);
  and and_25 (and_25_out, A4, A3);
  not not_31 (not_31_out, A4);
  not not_32 (not_32_out, A3);
  and and_26 (and_26_out, not_31_out, not_32_out, not_33_out);
  not not_33 (not_33_out, A1);
  not not_34 (not_34_out, A3);
  and and_27 (and_27_out, not_34_out, A2, A1);
  and and_28 (and_28_out, A3, not_35_out, A1);
  not not_35 (not_35_out, A2);
  and and_29 (and_29_out, A3, A2, not_36_out);
  not not_36 (not_36_out, A1);
  and and_30 (and_30_out, A4, not_37_out, not_38_out);
  not not_37 (not_37_out, A2);
  not not_38 (not_38_out, A1);
  not not_39 (not_39_out, A4);
  and and_31 (and_31_out, not_39_out, not_40_out);
  not not_40 (not_40_out, A2);
  not not_41 (not_41_out, A4);
  and and_32 (and_32_out, not_41_out, A1);
  not not_42 (not_42_out, A2);
  and and_33 (and_33_out, not_42_out, A1);
  not not_43 (not_43_out, A4);
  and and_34 (and_34_out, not_43_out, A3);
  and and_35 (and_35_out, A4, not_44_out);
  not not_44 (not_44_out, A3);
  or or_1 (L1, and_1_out, and_2_out, and_3_out, and_4_out, and_5_out);
  or or_2 (L3, and_12_out, and_13_out, and_14_out, and_15_out, and_16_out);
  or or_3 (L4, and_17_out, and_18_out, and_19_out, and_20_out, and_21_out);
  or or_4 (L5, and_22_out, and_23_out, and_24_out, and_25_out);
  or or_5 (L6, and_26_out, and_27_out, and_28_out, and_29_out, and_30_out);
  or or_6 (L7, and_31_out, and_32_out, and_33_out, and_34_out, and_35_out);
  or or_7 (L2, and_6_out, and_7_out, and_8_out, and_9_out, and_10_out, and_11_out);
endmodule

module calculadora (
  input  in_1,
  input  in_2,
  input  in_3,
  input  in_4
);

  wire decodificador_1_l1, decodificador_1_l2, decodificador_1_l3, decodificador_1_l4, decodificador_1_l5,
       decodificador_1_l6, decodificador_1_l7;

  Decodificador decodificador_1 (
    .A4(in_1), .A3(in_2), .A2(in_3), .A1(in_4), .L1(decodificador_1_l1), .L2(decodificador_1_l2),
    .L3(decodificador_1_l3), .L4(decodificador_1_l4), .L5(decodificador_1_l5), .L6(decodificador_1_l6),
    .L7(decodificador_1_l7));
  _7_Segment_Display u_7_segment_display_1 (
    .g(decodificador_1_l4), .f(decodificador_1_l3), .a(decodificador_1_l2), .b(decodificador_1_l1),
    .e(decodificador_1_l5), .d(decodificador_1_l6), .c(decodificador_1_l7));  // open: dp
endmodule
